// Logisim project myCPU256_evo.circ as structural Verilog: 6 circuits, main circuit myCPU256
module myCPU256 (
);

  wire AI, and_1_out, and_3_out, and_4_out, and_5_out, and_6_out, and_7_out, and_8_out, AO, BI, BO, CI, CLK,
       clock_1_out, CO, decoder_1_out0, decoder_1_out1, decoder_1_out2, decoder_1_out3, decoder_1_out4,
       decoder_1_out5, decoder_1_out6, decoder_1_out7, EO, FC, FI, FN, FV, FZ, HLT, II, IO, MI, not_1_out,
       OI, or_1_out, PE, PI, PO, RI, RO, RST, SI, SO, SQR, SU, switch_1_p2, switch_2_p2, UN;
  wire [3:0] ic245_1_o, ic245_1_o_2, register_1_q, register_2_q, register_2_q_2, register_3_q,
       register_3_q_2, register_4_q, register_4_q_2, register_5_q, register_5_q_2, register_6_q,
       register_6_q_2, register_7_q, register_7_q_2;
  wire [6:0] ic157_8b_1_out3;
  wire [7:0] alu_mycpu_1_r_out, counter_2_q, dipswitch_2_sw8, ic157_8b_3_out3, MEM1_data, MEM2_data,
       MEM3_data, ram_1_dout, undriven, undriven_2, undriven_3;
  wire [7:2] ic157_8b_2_out3;
  wire [14:0] pull_resistor_2_node;
  wire [14:14] pull_resistor_1_node, pull_resistor_3_node;

  Clock clock_1 (.out(clock_1_out));
  Pull_Resistor pull_resistor_1 (.node(pull_resistor_1_node[14]));
  Pull_Resistor pull_resistor_2 (.node(pull_resistor_2_node[14]));
  Pull_Resistor pull_resistor_3 (.node(pull_resistor_3_node[14]));
  and and_1 (and_1_out, ~FI, CLK);  // AND_Gate
  and and_2 (CLK, clock_1_out, ~HLT);  // AND_Gate
  Register #(.width(4)) register_1 (.D({FC, FN, FZ, FV}), .clk(and_1_out), .Q(register_1_q), .clr(RST));  // open: en
  // NoConnect on register_2_q[3]
  // NoConnect on register_2_q[2]
  Button button_1 (.out(RST));
  LED led_1 (.in(register_1_q[3]));
  LED led_2 (.in(register_1_q[2]));
  LED led_3 (.in(register_1_q[1]));
  LED led_4 (.in(register_1_q[0]));
  or or_1 (or_1_out, RST, SQR);
  ROM #(.addrWidth(17)) MEM3 (
    .addr({2'b11, {2{pull_resistor_1_node[14]}}, register_1_q, register_2_q[1:0], register_2_q_2, pull_resistor_2_node[2:0]}),
    .data(MEM3_data));
  ROM #(.addrWidth(17)) MEM2 (
    .addr({2'b10, {2{pull_resistor_2_node[14]}}, register_1_q, register_2_q[1:0], register_2_q_2, pull_resistor_2_node[2:0]}),
    .data(MEM2_data));
  ROM #(.addrWidth(17)) MEM1 (
    .addr({2'b01, {2{pull_resistor_3_node[14]}}, register_1_q, register_2_q[1:0], register_2_q_2, pull_resistor_2_node[2:0]}),
    .data(MEM1_data));
  Counter #(.max('h7), .trigger("falling"), .width(3)) counter_1 (
    .Q(pull_resistor_2_node[2:0]), .clk(CLK), .clr(or_1_out));  // open: load, D, count, carry, up
  LedBar ledbar_1 (
    .led0(decoder_1_out0), .led1(decoder_1_out1), .led2(decoder_1_out2), .led3(decoder_1_out3),
    .led4(decoder_1_out4), .led5(decoder_1_out5), .led6(decoder_1_out6), .led7(decoder_1_out7));
  Decoder #(.select(3)) decoder_1 (
    .out0(decoder_1_out0), .out1(decoder_1_out1), .out2(decoder_1_out2), .out3(decoder_1_out3),
    .out4(decoder_1_out4), .out5(decoder_1_out5), .out6(decoder_1_out6), .out7(decoder_1_out7),
    .sel(pull_resistor_2_node[2:0]));  // open: en
  Counter counter_2 (
    .clr(RST), .load(not_1_out), .count(PE), .clk(CLK), .D({ic245_1_o_2, ic245_1_o}), .Q(counter_2_q));  // open: up, carry
  not not_1 (not_1_out, PI);
  LedBar #(.matrixcols(24)) ledbar_2 (
    .led0(HLT), .led1(ic157_8b_1_out3[6]), .led2(SU), .led3(ic157_8b_1_out3[4]), .led4(ic157_8b_1_out3[3]),
    .led5(ic157_8b_1_out3[2]), .led6(ic157_8b_1_out3[1]), .led7(ic157_8b_1_out3[0]),
    .led8(ic157_8b_2_out3[7]), .led9(ic157_8b_2_out3[6]), .led10(ic157_8b_2_out3[5]),
    .led11(ic157_8b_2_out3[4]), .led12(ic157_8b_2_out3[3]), .led13(ic157_8b_2_out3[2]), .led14(PE),
    .led15(UN), .led16(ic157_8b_3_out3[7]), .led17(ic157_8b_3_out3[6]), .led18(RI),
    .led19(ic157_8b_3_out3[4]), .led20(ic157_8b_3_out3[3]), .led21(ic157_8b_3_out3[2]), .led22(SQR),
    .led23(ic157_8b_3_out3[0]));
  IC157_8b ic157_8b_1 (
    .IN3(undriven), .SEL(switch_1_p2), .M3(MEM3_data),
    .OUT3({HLT, ic157_8b_1_out3[6], SU, ic157_8b_1_out3[4:0]}));
  IC157_8b ic157_8b_2 (.IN3(undriven_2), .SEL(switch_1_p2), .M3(MEM2_data), .OUT3({ic157_8b_2_out3, PE, UN}));
  IC157_8b ic157_8b_3 (
    .IN3(undriven_3), .SEL(switch_1_p2), .M3(MEM1_data),
    .OUT3({ic157_8b_3_out3[7:6], RI, ic157_8b_3_out3[4:2], SQR, ic157_8b_3_out3[0]}));
  Register register_2 (
    .D({ic245_1_o_2, ic245_1_o}), .clk(and_3_out), .Q({register_2_q, register_2_q_2}), .clr(RST));  // open: en
  and and_3 (and_3_out, ~II, CLK);  // AND_Gate
  Hex_Digit_Display #(.decimalPoint("false")) hex_digit_display_1 (.value(register_2_q));
  Hex_Digit_Display #(.decimalPoint("false")) hex_digit_display_2 (.value(counter_2_q[7:4]));
  Hex_Digit_Display #(.decimalPoint("false")) hex_digit_display_3 (.value(register_2_q_2));
  // LedBar #(.inputtype("row")) ledbar_3: pin names not known; wires that end beside it: {register_2_q, register_2_q_2}
  // DipSwitch #(.number(24)) dipswitch_1: pin names not known
  // Switch switch_1: pin names not known; wires that end beside it: 1'b1, switch_1_p2
  Hex_Digit_Display #(.decimalPoint("false")) hex_digit_display_4 (.value(counter_2_q[3:0]));
  IC245 ic245_1 (.OE(PO), .I(counter_2_q), .O({ic245_1_o_2, ic245_1_o}));
  not not_2 (EO, ic157_8b_1_out3[6]);
  not not_3 (AO, ic157_8b_1_out3[4]);
  not not_4 (AI, ic157_8b_1_out3[3]);
  not not_5 (BO, ic157_8b_1_out3[2]);
  not not_6 (BI, ic157_8b_1_out3[1]);
  not not_7 (CO, ic157_8b_1_out3[0]);
  not not_8 (CI, ic157_8b_2_out3[7]);
  not not_9 (IO, ic157_8b_2_out3[6]);
  not not_10 (II, ic157_8b_2_out3[5]);
  not not_11 (FI, ic157_8b_2_out3[4]);
  not not_12 (PI, ic157_8b_2_out3[3]);
  not not_13 (PO, ic157_8b_2_out3[2]);
  not not_14 (OI, ic157_8b_3_out3[7]);
  not not_15 (RO, ic157_8b_3_out3[6]);
  not not_16 (SO, ic157_8b_3_out3[4]);
  not not_17 (SI, ic157_8b_3_out3[3]);
  not not_18 (MI, ic157_8b_3_out3[2]);
  // NoConnect on ic157_8b_3_out3[0]
  Pull_Resistor pull_resistor_4 (.node(switch_1_p2));
  DipSwitch dipswitch_2 (
    .sw1(dipswitch_2_sw8[7]), .sw2(dipswitch_2_sw8[6]), .sw3(dipswitch_2_sw8[5]), .sw4(dipswitch_2_sw8[4]),
    .sw5(dipswitch_2_sw8[3]), .sw6(dipswitch_2_sw8[2]), .sw7(dipswitch_2_sw8[1]), .sw8(dipswitch_2_sw8[0]));
  Hex_Digit_Display #(.decimalPoint("false")) hex_digit_display_5 (.value(register_3_q_2));
  Register register_3 (
    .D({ic245_1_o_2, ic245_1_o}), .clk(and_4_out), .Q({register_3_q_2, register_3_q}), .clr(RST));  // open: en
  and and_4 (and_4_out, ~AI, CLK);  // AND_Gate
  Hex_Digit_Display #(.decimalPoint("false")) hex_digit_display_6 (.value(register_4_q_2));
  Register register_4 (
    .D({ic245_1_o_2, ic245_1_o}), .clk(and_5_out), .Q({register_4_q_2, register_4_q}), .clr(RST));  // open: en
  and and_5 (and_5_out, ~MI, CLK);  // AND_Gate
  // Switch switch_2: pin names not known; wires that end beside it: 1'b0, switch_2_p2
  Hex_Digit_Display #(.decimalPoint("false")) hex_digit_display_7 (.value(register_3_q));
  Hex_Digit_Display #(.decimalPoint("false")) hex_digit_display_8 (.value(register_4_q));
  IC245 ic245_2 (.OE(switch_2_p2), .I(dipswitch_2_sw8), .O({ic245_1_o_2, ic245_1_o}));
  Pull_Resistor #(.pull(1)) pull_resistor_5 (.node(switch_2_p2));
  BTD btd_1 (.I({register_3_q_2, register_3_q}));
  IC245 ic245_3 (.OE(AO), .I({register_3_q_2, register_3_q}), .O({ic245_1_o_2, ic245_1_o}));
  RAM #(.trigger("falling"), .\type ("nonvolatile")) ram_1 (
    .addr({register_4_q_2, register_4_q}), .we(RI), .oe(1'b1), .clk(CLK), .din({ic245_1_o_2, ic245_1_o}),
    .dout(ram_1_dout));
  Hex_Digit_Display #(.decimalPoint("false")) hex_digit_display_9 (.value(ic245_1_o_2));
  Hex_Digit_Display #(.decimalPoint("false")) hex_digit_display_10 (.value(ic245_1_o));
  Register register_5 (
    .D({ic245_1_o_2, ic245_1_o}), .clk(and_6_out), .Q({register_5_q_2, register_5_q}), .clr(RST));  // open: en
  and and_6 (and_6_out, ~BI, CLK);  // AND_Gate
  BTD btd_2 (.I({ic245_1_o_2, ic245_1_o}));
  Hex_Digit_Display #(.decimalPoint("false")) hex_digit_display_11 (.value(register_5_q_2));
  Hex_Digit_Display #(.decimalPoint("false")) hex_digit_display_12 (.value(register_5_q));
  Hex_Digit_Display #(.decimalPoint("false")) hex_digit_display_13 (.value(ram_1_dout[7:4]));
  Hex_Digit_Display #(.decimalPoint("false")) hex_digit_display_14 (.value(ram_1_dout[3:0]));
  and and_7 (and_7_out, ~OI, CLK);  // AND_Gate
  BTD btd_3 (.I({register_5_q_2, register_5_q}));
  IC245 ic245_4 (.OE(BO), .I({register_5_q_2, register_5_q}), .O({ic245_1_o_2, ic245_1_o}));
  ALU_myCPU alu_mycpu_1 (
    .A_IN({register_3_q_2, register_3_q}), .B_IN({register_5_q_2, register_5_q}), .OPSEL(SU),
    .R_OUT(alu_mycpu_1_r_out), .CRY(FC), .OVF(FV), .NEG(FN), .ZERO(FZ));  // open: BRW
  Hex_Digit_Display #(.decimalPoint("false")) hex_digit_display_15 (.value(register_6_q_2));
  Register register_6 (
    .D({ic245_1_o_2, ic245_1_o}), .clk(and_7_out), .Q({register_6_q_2, register_6_q}), .clr(RST));  // open: en
  IC245 ic245_5 (.OE(RO), .I(ram_1_dout), .O({ic245_1_o_2, ic245_1_o}));
  Hex_Digit_Display #(.decimalPoint("false")) hex_digit_display_16 (.value(register_6_q));
  Hex_Digit_Display #(.decimalPoint("false")) hex_digit_display_17 (.value(register_7_q_2));
  Hex_Digit_Display #(.decimalPoint("false")) hex_digit_display_18 (.value(register_7_q));
  Register register_7 (
    .D({ic245_1_o_2, ic245_1_o}), .clk(and_8_out), .Q({register_7_q_2, register_7_q}), .clr(RST));  // open: en
  and and_8 (and_8_out, ~CI, CLK);  // AND_Gate
  BTD btd_4 (.I(alu_mycpu_1_r_out));
  IC245 ic245_6 (.OE(EO), .I(alu_mycpu_1_r_out), .O({ic245_1_o_2, ic245_1_o}));
  BTD btd_5 (.I({register_6_q_2, register_6_q}));
  BTD btd_6 (.I({register_7_q_2, register_7_q}));
  IC245 ic245_7 (.OE(CO), .I({register_7_q_2, register_7_q}), .O({ic245_1_o_2, ic245_1_o}));

  // Notes on the sheet:
  //   FLAGS
  //   CLOCK/HLT
  //   FLAGS REG
  //   INSTRUCTION DECODER (17b)
  //   OPCODE
  //   OPCODE
  //   FC
  //   FN
  //   STEP
  //   RESET
  //   FZ
  //   FV
  //   contents of MEM3 (hex, n*v repeats v):
  //   8192*0 4 40 2 5*0 4 40 4 44 40 2 0 0 4 40 4 44 40 0 2 0 4 40 4 44 40 0 2 0 4 40 4 44 20 2 0 0 4 40 4
  //   40 2 0 0 0 4 40 4 40 2 0 0 0 4 40 0 2 4*0 4 40 0 2 4*0 4 40 2 5*0 4 40 0 2 4*0 4 40 4 40 0 2 0 0 4
  //   40 4 40 0 2 0 0 4 40 2 5*0 4 40 80 2 4*0 4 40 390*0 4 40 2 5*0 4 40 4 44 40 2 0 0 4 40 4 44 40 0 2 0
  //   4 40 4 44 40 0 2 0 4 40 4 44 20 2 0 0 4 40 4 40 2 0 0 0 4 40 4 40 2 0 0 0 4 40 0 2 4*0 4 40 0 2 4*0
  //   4 40 2 5*0 4 40 0 2 4*0 4 40 4 40 0 2 0 0 4 40 4 40 0 2 0 0 4 40 2 5*0 4 40 80 2 4*0 4 40 390*0 4 40
  //   2 5*0 4 40 4 44 40 2 0 0 4 40 4 44 40 0 2 0 4 40 4 44 40 0 2 0 4 40 4 44 20 2 0 0 4 40 4 40 2 0 0 0
  //   4 40 4 40 2 0 0 0 4 40 0 2 4*0 4 40 4 40 2 0 0 0 4 40 2 5*0 4 40 0 2 4*0 4 40 4 40 0 2 0 0 4 40 4 40
  //   0 2 0 0 4 40 2 5*0 4 40 80 2 4*0 4 40 390*0 4 40 2 5*0 4 40 4 44 40 2 0 0 4 40 4 44 40 0 2 0 4 40 4
  //   44 40 0 2 0 4 40 4 44 20 2 0 0 4 40 4 40 2 0 0 0 4 40 4 40 2 0 0 0 4 40 0 2 4*0 4 40 4 40 2 0 0 0 4
  //   40 2 5*0 4 40 0 2 4*0 4 40 4 40 0 2 0 0 4 40 4 40 0 2 0 0 4 40 2 5*0 4 40 80 2 4*0 4 40 390*0 4 40 2
  //   5*0 4 40 4 44 40 2 0 0 4 40 4 44 40 0 2 0 4 40 4 44 40 0 2 0 4 40 4 44 20 2 0 0 4 40 4 40 2 0 0 0 4
  //   40 4 40 2 0 0 0 4 40 0 2 4*0 4 40 0 2 4*0 4 40 2 5*0 4 40 0 2 4*0 4 40 4 40 0 2 0 0 4 40 4 40 0 2 0
  //   0 4 40 2 5*0 4 40 80 2 4*0 4 40 390*0 4 40 2 5*0 4 40 4 44 40 2 0 0 4 40 4 44 40 0 2 0 4 40 4 44 40
  //   0 2 0 4 40 4 44 20 2 0 0 4 40 4 40 2 0 0 0 4 40 4 40 2 0 0 0 4 40 0 2 4*0 4 40 0 2 4*0 4 40 2 5*0 4
  //   40 0 2 4*0 4 40 4 40 0 2 0 0 4 40 4 40 0 2 0 0 4 40 2 5*0 4 40 80 2 4*0 4 40 390*0 4 40 2 5*0 4 40 4
  //   44 40 2 0 0 4 40 4 44 40 0 2 0 4 40 4 44 40 0 2 0 4 40 4 44 20 2 0 0 4 40 4 40 2 0 0 0 4 40 4 40 2 0
  //   0 0 4 40 0 2 4*0 4 40 4 40 2 0 0 0 4 40 2 5*0 4 40 0 2 4*0 4 40 4 40 0 2 0 0 4 40 4 40 0 2 0 0 4 40
  //   2 5*0 4 40 80 2 4*0 4 40 390*0 4 40 2 5*0 4 40 4 44 40 2 0 0 4 40 4 44 40 0 2 0 4 40 4 44 40 0 2 0 4
  //   40 4 44 20 2 0 0 4 40 4 40 2 0 0 0 4 40 4 40 2 0 0 0 4 40 0 2 4*0 4 40 4 40 2 0 0 0 4 40 2 5*0 4 40
  //   0 2 4*0 4 40 4 40 0 2 0 0 4 40 4 40 0 2 0 0 4 40 2 5*0 4 40 80 2 4*0 4 40 390*0 4 40 2 5*0 4 40 4 44
  //   40 2 0 0 4 40 4 44 40 0 2 0 4 40 4 44 40 0 2 0 4 40 4 44 20 2 0 0 4 40 4 40 2 0 0 0 4 40 4 40 2 0 0
  //   0 4 40 4 40 2 0 0 0 4 40 0 2 4*0 4 40 2 5*0 4 40 0 2 4*0 4 40 4 40 0 2 0 0 4 40 4 40 0 2 0 0 4 40 2
  //   5*0 4 40 80 2 4*0 4 40 390*0 4 40 2 5*0 4 40 4 44 40 2 0 0 4 40 4 44 40 0 2 0 4 40 4 44 40 0 2 0 4
  //   40 4 44 20 2 0 0 4 40 4 40 2 0 0 0 4 40 4 40 2 0 0 0 4 40 4 40 2 0 0 0 4 40 0 2 4*0 4 40 2 5*0 4 40
  //   0 2 4*0 4 40 4 40 0 2 0 0 4 40 4 40 0 2 0 0 4 40 2 5*0 4 40 80 2 4*0 4 40 390*0 4 40 2 5*0 4 40 4 44
  //   40 2 0 0 4 40 4 44 40 0 2 0 4 40 4 44 40 0 2 0 4 40 4 44 20 2 0 0 4 40 4 40 2 0 0 0 4 40 4 40 2 0 0
  //   0 4 40 4 40 2 0 0 0 4 40 4 40 2 0 0 0 4 40 2 5*0 4 40 0 2 4*0 4 40 4 40 0 2 0 0 4 40 4 40 0 2 0 0 4
  //   40 2 5*0 4 40 80 2 4*0 4 40 390*0 4 40 2 5*0 4 40 4 44 40 2 0 0 4 40 4 44 40 0 2 0 4 40 4 44 40 0 2
  //   0 4 40 4 44 20 2 0 0 4 40 4 40 2 0 0 0 4 40 4 40 2 0 0 0 4 40 4 40 2 0 0 0 4 40 4 40 2 0 0 0 4 40 2
  //   5*0 4 40 0 2 4*0 4 40 4 40 0 2 0 0 4 40 4 40 0 2 0 0 4 40 2 5*0 4 40 80 2 4*0 4 40 390*0 4 40 2 5*0
  //   4 40 4 44 40 2 0 0 4 40 4 44 40 0 2 0 4 40 4 44 40 0 2 0 4 40 4 44 20 2 0 0 4 40 4 40 2 0 0 0 4 40 4
  //   40 2 0 0 0 4 40 4 40 2 0 0 0 4 40 0 2 4*0 4 40 2 5*0 4 40 0 2 4*0 4 40 4 40 0 2 0 0 4 40 4 40 0 2 0
  //   0 4 40 2 5*0 4 40 80 2 4*0 4 40 390*0 4 40 2 5*0 4 40 4 44 40 2 0 0 4 40 4 44 40 0 2 0 4 40 4 44 40
  //   0 2 0 4 40 4 44 20 2 0 0 4 40 4 40 2 0 0 0 4 40 4 40 2 0 0 0 4 40 4 40 2 0 0 0 4 40 0 2 4*0 4 40 2
  //   5*0 4 40 0 2 4*0 4 40 4 40 0 2 0 0 4 40 4 40 0 2 0 0 4 40 2 5*0 4 40 80 2 4*0 4 40 390*0 4 40 2 5*0
  //   4 40 4 44 40 2 0 0 4 40 4 44 40 0 2 0 4 40 4 44 40 0 2 0 4 40 4 44 20 2 0 0 4 40 4 40 2 0 0 0 4 40 4
  //   40 2 0 0 0 4 40 4 40 2 0 0 0 4 40 4 40 2 0 0 0 4 40 2 5*0 4 40 0 2 4*0 4 40 4 40 0 2 0 0 4 40 4 40 0
  //   2 0 0 4 40 2 5*0 4 40 80 2 4*0 4 40 390*0 4 40 2 5*0 4 40 4 44 40 2 0 0 4 40 4 44 40 0 2 0 4 40 4 44
  //   40 0 2 0 4 40 4 44 20 2 0 0 4 40 4 40 2 0 0 0 4 40 4 40 2 0 0 0 4 40 4 40 2 0 0 0 4 40 4 40 2 0 0 0
  //   4 40 2 5*0 4 40 0 2 4*0 4 40 4 40 0 2 0 0 4 40 4 40 0 2 0 0 4 40 2 5*0 4 40 80 2 4*0 4 40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
  //   contents of MEM2 (hex, n*v repeats v):
  //   8192*0 4 40 2 5*0 4 40 4 44 40 2 0 0 4 40 4 44 40 0 2 0 4 40 4 44 40 0 2 0 4 40 4 44 20 2 0 0 4 40 4
  //   40 2 0 0 0 4 40 4 40 2 0 0 0 4 40 0 2 4*0 4 40 0 2 4*0 4 40 2 5*0 4 40 0 2 4*0 4 40 4 40 0 2 0 0 4
  //   40 4 40 0 2 0 0 4 40 2 5*0 4 40 80 2 4*0 4 40 390*0 4 40 2 5*0 4 40 4 44 40 2 0 0 4 40 4 44 40 0 2 0
  //   4 40 4 44 40 0 2 0 4 40 4 44 20 2 0 0 4 40 4 40 2 0 0 0 4 40 4 40 2 0 0 0 4 40 0 2 4*0 4 40 0 2 4*0
  //   4 40 2 5*0 4 40 0 2 4*0 4 40 4 40 0 2 0 0 4 40 4 40 0 2 0 0 4 40 2 5*0 4 40 80 2 4*0 4 40 390*0 4 40
  //   2 5*0 4 40 4 44 40 2 0 0 4 40 4 44 40 0 2 0 4 40 4 44 40 0 2 0 4 40 4 44 20 2 0 0 4 40 4 40 2 0 0 0
  //   4 40 4 40 2 0 0 0 4 40 0 2 4*0 4 40 4 40 2 0 0 0 4 40 2 5*0 4 40 0 2 4*0 4 40 4 40 0 2 0 0 4 40 4 40
  //   0 2 0 0 4 40 2 5*0 4 40 80 2 4*0 4 40 390*0 4 40 2 5*0 4 40 4 44 40 2 0 0 4 40 4 44 40 0 2 0 4 40 4
  //   44 40 0 2 0 4 40 4 44 20 2 0 0 4 40 4 40 2 0 0 0 4 40 4 40 2 0 0 0 4 40 0 2 4*0 4 40 4 40 2 0 0 0 4
  //   40 2 5*0 4 40 0 2 4*0 4 40 4 40 0 2 0 0 4 40 4 40 0 2 0 0 4 40 2 5*0 4 40 80 2 4*0 4 40 390*0 4 40 2
  //   5*0 4 40 4 44 40 2 0 0 4 40 4 44 40 0 2 0 4 40 4 44 40 0 2 0 4 40 4 44 20 2 0 0 4 40 4 40 2 0 0 0 4
  //   40 4 40 2 0 0 0 4 40 0 2 4*0 4 40 0 2 4*0 4 40 2 5*0 4 40 0 2 4*0 4 40 4 40 0 2 0 0 4 40 4 40 0 2 0
  //   0 4 40 2 5*0 4 40 80 2 4*0 4 40 390*0 4 40 2 5*0 4 40 4 44 40 2 0 0 4 40 4 44 40 0 2 0 4 40 4 44 40
  //   0 2 0 4 40 4 44 20 2 0 0 4 40 4 40 2 0 0 0 4 40 4 40 2 0 0 0 4 40 0 2 4*0 4 40 0 2 4*0 4 40 2 5*0 4
  //   40 0 2 4*0 4 40 4 40 0 2 0 0 4 40 4 40 0 2 0 0 4 40 2 5*0 4 40 80 2 4*0 4 40 390*0 4 40 2 5*0 4 40 4
  //   44 40 2 0 0 4 40 4 44 40 0 2 0 4 40 4 44 40 0 2 0 4 40 4 44 20 2 0 0 4 40 4 40 2 0 0 0 4 40 4 40 2 0
  //   0 0 4 40 0 2 4*0 4 40 4 40 2 0 0 0 4 40 2 5*0 4 40 0 2 4*0 4 40 4 40 0 2 0 0 4 40 4 40 0 2 0 0 4 40
  //   2 5*0 4 40 80 2 4*0 4 40 390*0 4 40 2 5*0 4 40 4 44 40 2 0 0 4 40 4 44 40 0 2 0 4 40 4 44 40 0 2 0 4
  //   40 4 44 20 2 0 0 4 40 4 40 2 0 0 0 4 40 4 40 2 0 0 0 4 40 0 2 4*0 4 40 4 40 2 0 0 0 4 40 2 5*0 4 40
  //   0 2 4*0 4 40 4 40 0 2 0 0 4 40 4 40 0 2 0 0 4 40 2 5*0 4 40 80 2 4*0 4 40 390*0 4 40 2 5*0 4 40 4 44
  //   40 2 0 0 4 40 4 44 40 0 2 0 4 40 4 44 40 0 2 0 4 40 4 44 20 2 0 0 4 40 4 40 2 0 0 0 4 40 4 40 2 0 0
  //   0 4 40 4 40 2 0 0 0 4 40 0 2 4*0 4 40 2 5*0 4 40 0 2 4*0 4 40 4 40 0 2 0 0 4 40 4 40 0 2 0 0 4 40 2
  //   5*0 4 40 80 2 4*0 4 40 390*0 4 40 2 5*0 4 40 4 44 40 2 0 0 4 40 4 44 40 0 2 0 4 40 4 44 40 0 2 0 4
  //   40 4 44 20 2 0 0 4 40 4 40 2 0 0 0 4 40 4 40 2 0 0 0 4 40 4 40 2 0 0 0 4 40 0 2 4*0 4 40 2 5*0 4 40
  //   0 2 4*0 4 40 4 40 0 2 0 0 4 40 4 40 0 2 0 0 4 40 2 5*0 4 40 80 2 4*0 4 40 390*0 4 40 2 5*0 4 40 4 44
  //   40 2 0 0 4 40 4 44 40 0 2 0 4 40 4 44 40 0 2 0 4 40 4 44 20 2 0 0 4 40 4 40 2 0 0 0 4 40 4 40 2 0 0
  //   0 4 40 4 40 2 0 0 0 4 40 4 40 2 0 0 0 4 40 2 5*0 4 40 0 2 4*0 4 40 4 40 0 2 0 0 4 40 4 40 0 2 0 0 4
  //   40 2 5*0 4 40 80 2 4*0 4 40 390*0 4 40 2 5*0 4 40 4 44 40 2 0 0 4 40 4 44 40 0 2 0 4 40 4 44 40 0 2
  //   0 4 40 4 44 20 2 0 0 4 40 4 40 2 0 0 0 4 40 4 40 2 0 0 0 4 40 4 40 2 0 0 0 4 40 4 40 2 0 0 0 4 40 2
  //   5*0 4 40 0 2 4*0 4 40 4 40 0 2 0 0 4 40 4 40 0 2 0 0 4 40 2 5*0 4 40 80 2 4*0 4 40 390*0 4 40 2 5*0
  //   4 40 4 44 40 2 0 0 4 40 4 44 40 0 2 0 4 40 4 44 40 0 2 0 4 40 4 44 20 2 0 0 4 40 4 40 2 0 0 0 4 40 4
  //   40 2 0 0 0 4 40 4 40 2 0 0 0 4 40 0 2 4*0 4 40 2 5*0 4 40 0 2 4*0 4 40 4 40 0 2 0 0 4 40 4 40 0 2 0
  //   0 4 40 2 5*0 4 40 80 2 4*0 4 40 390*0 4 40 2 5*0 4 40 4 44 40 2 0 0 4 40 4 44 40 0 2 0 4 40 4 44 40
  //   0 2 0 4 40 4 44 20 2 0 0 4 40 4 40 2 0 0 0 4 40 4 40 2 0 0 0 4 40 4 40 2 0 0 0 4 40 0 2 4*0 4 40 2
  //   5*0 4 40 0 2 4*0 4 40 4 40 0 2 0 0 4 40 4 40 0 2 0 0 4 40 2 5*0 4 40 80 2 4*0 4 40 390*0 4 40 2 5*0
  //   4 40 4 44 40 2 0 0 4 40 4 44 40 0 2 0 4 40 4 44 40 0 2 0 4 40 4 44 20 2 0 0 4 40 4 40 2 0 0 0 4 40 4
  //   40 2 0 0 0 4 40 4 40 2 0 0 0 4 40 4 40 2 0 0 0 4 40 2 5*0 4 40 0 2 4*0 4 40 4 40 0 2 0 0 4 40 4 40 0
  //   2 0 0 4 40 2 5*0 4 40 80 2 4*0 4 40 390*0 4 40 2 5*0 4 40 4 44 40 2 0 0 4 40 4 44 40 0 2 0 4 40 4 44
  //   40 0 2 0 4 40 4 44 20 2 0 0 4 40 4 40 2 0 0 0 4 40 4 40 2 0 0 0 4 40 4 40 2 0 0 0 4 40 4 40 2 0 0 0
  //   4 40 2 5*0 4 40 0 2 4*0 4 40 4 40 0 2 0 0 4 40 4 40 0 2 0 0 4 40 2 5*0 4 40 80 2 4*0 4 40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
  //   contents of MEM1 (hex, n*v repeats v):
  //   8192*0 4 40 2 5*0 4 40 4 44 40 2 0 0 4 40 4 44 40 0 2 0 4 40 4 44 40 0 2 0 4 40 4 44 20 2 0 0 4 40 4
  //   40 2 0 0 0 4 40 4 40 2 0 0 0 4 40 0 2 4*0 4 40 0 2 4*0 4 40 2 5*0 4 40 0 2 4*0 4 40 4 40 0 2 0 0 4
  //   40 4 40 0 2 0 0 4 40 2 5*0 4 40 80 2 4*0 4 40 390*0 4 40 2 5*0 4 40 4 44 40 2 0 0 4 40 4 44 40 0 2 0
  //   4 40 4 44 40 0 2 0 4 40 4 44 20 2 0 0 4 40 4 40 2 0 0 0 4 40 4 40 2 0 0 0 4 40 0 2 4*0 4 40 0 2 4*0
  //   4 40 2 5*0 4 40 0 2 4*0 4 40 4 40 0 2 0 0 4 40 4 40 0 2 0 0 4 40 2 5*0 4 40 80 2 4*0 4 40 390*0 4 40
  //   2 5*0 4 40 4 44 40 2 0 0 4 40 4 44 40 0 2 0 4 40 4 44 40 0 2 0 4 40 4 44 20 2 0 0 4 40 4 40 2 0 0 0
  //   4 40 4 40 2 0 0 0 4 40 0 2 4*0 4 40 4 40 2 0 0 0 4 40 2 5*0 4 40 0 2 4*0 4 40 4 40 0 2 0 0 4 40 4 40
  //   0 2 0 0 4 40 2 5*0 4 40 80 2 4*0 4 40 390*0 4 40 2 5*0 4 40 4 44 40 2 0 0 4 40 4 44 40 0 2 0 4 40 4
  //   44 40 0 2 0 4 40 4 44 20 2 0 0 4 40 4 40 2 0 0 0 4 40 4 40 2 0 0 0 4 40 0 2 4*0 4 40 4 40 2 0 0 0 4
  //   40 2 5*0 4 40 0 2 4*0 4 40 4 40 0 2 0 0 4 40 4 40 0 2 0 0 4 40 2 5*0 4 40 80 2 4*0 4 40 390*0 4 40 2
  //   5*0 4 40 4 44 40 2 0 0 4 40 4 44 40 0 2 0 4 40 4 44 40 0 2 0 4 40 4 44 20 2 0 0 4 40 4 40 2 0 0 0 4
  //   40 4 40 2 0 0 0 4 40 0 2 4*0 4 40 0 2 4*0 4 40 2 5*0 4 40 0 2 4*0 4 40 4 40 0 2 0 0 4 40 4 40 0 2 0
  //   0 4 40 2 5*0 4 40 80 2 4*0 4 40 390*0 4 40 2 5*0 4 40 4 44 40 2 0 0 4 40 4 44 40 0 2 0 4 40 4 44 40
  //   0 2 0 4 40 4 44 20 2 0 0 4 40 4 40 2 0 0 0 4 40 4 40 2 0 0 0 4 40 0 2 4*0 4 40 0 2 4*0 4 40 2 5*0 4
  //   40 0 2 4*0 4 40 4 40 0 2 0 0 4 40 4 40 0 2 0 0 4 40 2 5*0 4 40 80 2 4*0 4 40 390*0 4 40 2 5*0 4 40 4
  //   44 40 2 0 0 4 40 4 44 40 0 2 0 4 40 4 44 40 0 2 0 4 40 4 44 20 2 0 0 4 40 4 40 2 0 0 0 4 40 4 40 2 0
  //   0 0 4 40 0 2 4*0 4 40 4 40 2 0 0 0 4 40 2 5*0 4 40 0 2 4*0 4 40 4 40 0 2 0 0 4 40 4 40 0 2 0 0 4 40
  //   2 5*0 4 40 80 2 4*0 4 40 390*0 4 40 2 5*0 4 40 4 44 40 2 0 0 4 40 4 44 40 0 2 0 4 40 4 44 40 0 2 0 4
  //   40 4 44 20 2 0 0 4 40 4 40 2 0 0 0 4 40 4 40 2 0 0 0 4 40 0 2 4*0 4 40 4 40 2 0 0 0 4 40 2 5*0 4 40
  //   0 2 4*0 4 40 4 40 0 2 0 0 4 40 4 40 0 2 0 0 4 40 2 5*0 4 40 80 2 4*0 4 40 390*0 4 40 2 5*0 4 40 4 44
  //   40 2 0 0 4 40 4 44 40 0 2 0 4 40 4 44 40 0 2 0 4 40 4 44 20 2 0 0 4 40 4 40 2 0 0 0 4 40 4 40 2 0 0
  //   0 4 40 4 40 2 0 0 0 4 40 0 2 4*0 4 40 2 5*0 4 40 0 2 4*0 4 40 4 40 0 2 0 0 4 40 4 40 0 2 0 0 4 40 2
  //   5*0 4 40 80 2 4*0 4 40 390*0 4 40 2 5*0 4 40 4 44 40 2 0 0 4 40 4 44 40 0 2 0 4 40 4 44 40 0 2 0 4
  //   40 4 44 20 2 0 0 4 40 4 40 2 0 0 0 4 40 4 40 2 0 0 0 4 40 4 40 2 0 0 0 4 40 0 2 4*0 4 40 2 5*0 4 40
  //   0 2 4*0 4 40 4 40 0 2 0 0 4 40 4 40 0 2 0 0 4 40 2 5*0 4 40 80 2 4*0 4 40 390*0 4 40 2 5*0 4 40 4 44
  //   40 2 0 0 4 40 4 44 40 0 2 0 4 40 4 44 40 0 2 0 4 40 4 44 20 2 0 0 4 40 4 40 2 0 0 0 4 40 4 40 2 0 0
  //   0 4 40 4 40 2 0 0 0 4 40 4 40 2 0 0 0 4 40 2 5*0 4 40 0 2 4*0 4 40 4 40 0 2 0 0 4 40 4 40 0 2 0 0 4
  //   40 2 5*0 4 40 80 2 4*0 4 40 390*0 4 40 2 5*0 4 40 4 44 40 2 0 0 4 40 4 44 40 0 2 0 4 40 4 44 40 0 2
  //   0 4 40 4 44 20 2 0 0 4 40 4 40 2 0 0 0 4 40 4 40 2 0 0 0 4 40 4 40 2 0 0 0 4 40 4 40 2 0 0 0 4 40 2
  //   5*0 4 40 0 2 4*0 4 40 4 40 0 2 0 0 4 40 4 40 0 2 0 0 4 40 2 5*0 4 40 80 2 4*0 4 40 390*0 4 40 2 5*0
  //   4 40 4 44 40 2 0 0 4 40 4 44 40 0 2 0 4 40 4 44 40 0 2 0 4 40 4 44 20 2 0 0 4 40 4 40 2 0 0 0 4 40 4
  //   40 2 0 0 0 4 40 4 40 2 0 0 0 4 40 0 2 4*0 4 40 2 5*0 4 40 0 2 4*0 4 40 4 40 0 2 0 0 4 40 4 40 0 2 0
  //   0 4 40 2 5*0 4 40 80 2 4*0 4 40 390*0 4 40 2 5*0 4 40 4 44 40 2 0 0 4 40 4 44 40 0 2 0 4 40 4 44 40
  //   0 2 0 4 40 4 44 20 2 0 0 4 40 4 40 2 0 0 0 4 40 4 40 2 0 0 0 4 40 4 40 2 0 0 0 4 40 0 2 4*0 4 40 2
  //   5*0 4 40 0 2 4*0 4 40 4 40 0 2 0 0 4 40 4 40 0 2 0 0 4 40 2 5*0 4 40 80 2 4*0 4 40 390*0 4 40 2 5*0
  //   4 40 4 44 40 2 0 0 4 40 4 44 40 0 2 0 4 40 4 44 40 0 2 0 4 40 4 44 20 2 0 0 4 40 4 40 2 0 0 0 4 40 4
  //   40 2 0 0 0 4 40 4 40 2 0 0 0 4 40 4 40 2 0 0 0 4 40 2 5*0 4 40 0 2 4*0 4 40 4 40 0 2 0 0 4 40 4 40 0
  //   2 0 0 4 40 2 5*0 4 40 80 2 4*0 4 40 390*0 4 40 2 5*0 4 40 4 44 40 2 0 0 4 40 4 44 40 0 2 0 4 40 4 44
  //   40 0 2 0 4 40 4 44 20 2 0 0 4 40 4 40 2 0 0 0 4 40 4 40 2 0 0 0 4 40 4 40 2 0 0 0 4 40 4 40 2 0 0 0
  //   4 40 2 5*0 4 40 0 2 4*0 4 40 4 40 0 2 0 0 4 40 4 40 0 2 0 0 4 40 2 5*0 4 40 80 2 4*0 4 40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
  //   SEQUENCER
  //   PROGRAM COUNTER
  //   HLT
  //   SU
  //   AI
  //   EO
  //   AO
  //   BO
  //   INSTRUCTION REG
  //   BI
  //   CI
  //   II
  //   PI
  //   CO
  //   IO
  //   FI
  //   PO
  //   CSM
  //   HEX
  //   PE
  //   OI
  //   RI
  //   SI
  //   UN
  //   RO
  //   SO
  //   MI
  //   SQR
  //   MICROINSTRUCTION
  //   A-REG ACC
  //   MAR
  //   HEX
  //   BUS MANAGER
  //   SRAM
  //   HEX
  //   B-REG
  //   ALU
  //   HEX
  //   OUTPUT REG
  //   C-REG
endmodule

module IC245 (
  input  [7:0] I,
  input  OE,
  output [7:0] O
);

  wire n74245_1_pin1;

  _74245 u_74245_1 (
    .pin1(n74245_1_pin1), .pin2(O[7]), .pin3(O[6]), .pin4(O[5]), .pin5(O[4]), .pin6(O[3]), .pin7(O[2]),
    .pin8(O[1]), .pin9(O[0]), .pin19(OE), .pin18(I[7]), .pin17(I[6]), .pin16(I[5]), .pin15(I[4]),
    .pin14(I[3]), .pin13(I[2]), .pin12(I[1]), .pin11(I[0]));
  // also tied to GND on the sheet: n74245_1_pin1

  // Notes on the sheet:
  //   OE: pull=up
endmodule

module BTD (
  input  [7:0] I
);

  wire n7_segment_display_1_p1, n7_segment_display_1_p2, n7_segment_display_2_p2;

  // _7_Segment_Display 7_segment_display_1: pin names not known; wires that end beside it: n7_segment_display_1_p1, n7_segment_display_1_p2
  // _7_Segment_Display 7_segment_display_2: pin names not known; wires that end beside it: n7_segment_display_1_p2, n7_segment_display_2_p2
  // BCD_to_7_Segment_decoder bcd_to_7_segment_decoder_1: pin names not known
  // BCD_to_7_Segment_decoder bcd_to_7_segment_decoder_2: pin names not known
  // Binary_to_BCD_converter #(.binvalue(8)) binary_to_bcd_converter_1: pin names not known; wires that end beside it: I, n7_segment_display_1_p1, n7_segment_display_1_p2
  _7_Segment_Display u_7_segment_display_3 ();  // open: g, f, a, b, e, d, c, dp
  // BCD_to_7_Segment_decoder bcd_to_7_segment_decoder_3: pin names not known; wires that end beside it: n7_segment_display_2_p2
endmodule

module ALU_myCPU (
  input  [7:0] A_IN,
  input  [7:0] B_IN,
  input  OPSEL,
  output NEG,
  output CRY,
  output [7:0] R_OUT,
  output ZERO,
  output BRW,
  output OVF
);

  wire IC_HIGHER_pin15;
  wire [7:0] adder_1_out, subtractor_1_out;

  Adder adder_1 (.a(A_IN), .b(B_IN), .out(adder_1_out), .cout(CRY));  // open: cin
  Subtractor subtractor_1 (.a(A_IN), .b(B_IN), .out(subtractor_1_out), .bout(BRW));  // open: bin
  _74157 #(.ShowInternalStructure("true")) IC_HIGHER (
    .pin1(OPSEL), .pin2(adder_1_out[0]), .pin3(subtractor_1_out[0]), .pin4(R_OUT[0]), .pin5(adder_1_out[1]),
    .pin6(subtractor_1_out[1]), .pin7(R_OUT[1]), .pin15(IC_HIGHER_pin15), .pin14(adder_1_out[3]),
    .pin13(subtractor_1_out[3]), .pin12(R_OUT[3]), .pin11(adder_1_out[2]), .pin10(subtractor_1_out[2]),
    .pin9(R_OUT[2]));
  _74157 #(.ShowInternalStructure("true")) IC_LOWER (
    .pin1(OPSEL), .pin2(adder_1_out[4]), .pin3(subtractor_1_out[4]), .pin4(R_OUT[4]), .pin5(adder_1_out[5]),
    .pin6(subtractor_1_out[5]), .pin7(R_OUT[5]), .pin15(IC_HIGHER_pin15), .pin14(adder_1_out[7]),
    .pin13(subtractor_1_out[7]), .pin12(NEG), .pin11(adder_1_out[6]), .pin10(subtractor_1_out[6]),
    .pin9(R_OUT[6]));
  nor nor_1 (ZERO, NEG, R_OUT[6], R_OUT[5], R_OUT[4], R_OUT[3], R_OUT[2], R_OUT[1], R_OUT[0]);

  assign OVF = 1'b0;
  assign R_OUT[7] = NEG;
  // also tied to GND on the sheet: IC_HIGHER_pin15
endmodule

module IC245_4b (
  input  [7:0] I,
  input  OE,
  output [7:0] O
);

  wire n74245_1_pin1, n74245_1_pin15, n74245_1_pin16, n74245_1_pin17, n74245_1_pin18;

  _74245 #(.ShowInternalStructure("true")) u_74245_1 (
    .pin1(n74245_1_pin1), .pin2(O[7]), .pin3(O[6]), .pin4(O[5]), .pin5(O[4]), .pin6(O[3]), .pin7(O[2]),
    .pin8(O[1]), .pin9(O[0]), .pin19(OE), .pin18(n74245_1_pin18), .pin17(n74245_1_pin17),
    .pin16(n74245_1_pin16), .pin15(n74245_1_pin15), .pin14(I[3]), .pin13(I[2]), .pin12(I[1]), .pin11(I[0]));
  // also tied to GND on the sheet: {n74245_1_pin1, n74245_1_pin18, n74245_1_pin17, n74245_1_pin16, n74245_1_pin15}

  // Notes on the sheet:
  //   OE: pull=up
endmodule

module IC157_8b (
  input  SEL,
  input  [7:0] M3,
  input  [7:0] IN3,
  output [7:0] OUT3
);

  wire n74157_1_pin15;

  _74157 #(.ShowInternalStructure("true")) u_74157_1 (
    .pin1(SEL), .pin2(M3[4]), .pin3(IN3[4]), .pin4(OUT3[4]), .pin5(M3[5]), .pin6(IN3[5]), .pin7(OUT3[5]),
    .pin15(n74157_1_pin15), .pin14(M3[7]), .pin13(IN3[7]), .pin12(OUT3[7]), .pin11(M3[6]), .pin10(IN3[6]),
    .pin9(OUT3[6]));
  _74157 #(.ShowInternalStructure("true")) u_74157_2 (
    .pin1(SEL), .pin2(M3[0]), .pin3(IN3[0]), .pin4(OUT3[0]), .pin5(M3[1]), .pin6(IN3[1]), .pin7(OUT3[1]),
    .pin15(n74157_1_pin15), .pin14(M3[3]), .pin13(IN3[3]), .pin12(OUT3[3]), .pin11(M3[2]), .pin10(IN3[2]),
    .pin9(OUT3[2]));
  // also tied to GND on the sheet: n74157_1_pin15
endmodule
